// Logisim project esquema.circ as structural Verilog: 1 circuit, main circuit main
module main (
  input  A,
  input  B,
  input  C,
  input  D,
  output F1,
  output F2,
  output F3
);

  wire and_1_out, and_2_out, and_3_out, and_4_out, and_5_out, not_1_out, not_2_out, not_4_out;

  not not_1 (not_1_out, A);
  not not_2 (not_2_out, B);
  not not_3 (F2, C);
  not not_4 (not_4_out, D);
  and and_1 (and_1_out, B, C);
  and and_2 (and_2_out, A, C);
  and and_3 (and_3_out, not_1_out, not_2_out, F2);
  and and_4 (and_4_out, not_1_out, D);
  and and_5 (and_5_out, A, C, not_4_out);
  or or_1 (F1, and_1_out, and_2_out, and_3_out);
  or or_2 (F3, and_4_out, and_5_out, not_2_out);
endmodule
