// Logisim project Actividad3.circ as structural Verilog: 1 circuit, main circuit Sumador
module Sumador (
  input  A,
  input  B,
  input  C,
  output Ci,
  output s
);

  wire and_1_out, and_2_out, and_3_out;

  and and_1 (and_1_out, A, B);
  and and_2 (and_2_out, A, C);
  and and_3 (and_3_out, B, C);
  or or_1 (Ci, and_1_out, and_2_out, and_3_out);
  buf xor_1 (s, C);  // XOR_Gate
endmodule
